# Fritzing sketch Wire Connection (saved by Fritzing 0.9.3b)

parts:
  PWM1 = PCA9685 16x12-bit PWM Breakout
  Raspberry_Pi_1 = Raspberry Pi 3 [part_number=RPI-3-V1.2]
  J1 = Basic Servo
  DJI_ESC_30A2 = DJI 30A ESC
  920KV_Motor2 = DJI 920 KV Motor

nets:
  N1: PWM1.no_name_yet#0, J1.pulse
  N2: PWM1.no_name_yet#1, DJI_ESC_30A2.DATA
  N3: PWM1.no_name_yet#100, PWM1.no_name_yet#101, DJI_ESC_30A2.PWR_OUT
  GND: PWM1.no_name_yet#501, PWM1.no_name_yet#1000, PWM1.no_name_yet#1001, Raspberry_Pi_1.GND, DJI_ESC_30A2.GND
  N4: PWM1.no_name_yet#503, Raspberry_Pi_1.GPIO3
  N5: PWM1.no_name_yet#504, Raspberry_Pi_1.GPIO2
  N6: PWM1.no_name_yet#505, Raspberry_Pi_1.3v3
  N7: DJI_ESC_30A2.U, 920KV_Motor2.v
  N8: DJI_ESC_30A2.V, 920KV_Motor2.u
  N9: DJI_ESC_30A2.W, 920KV_Motor2.w

custom parts:
  DJI 920 KV Motor: DJI Brushless Outrunner 2212/920K Motor F330-550
